# Fritzing sketch PlusHomefzz (saved by Fritzing 0.9.3b)
circuit board: 4.5cm x 8.5cm
breadboards: 1

parts:
  HLK-PM1 = HLK-PM01
  IC1 = Voltage Regulator AMS1117 [package=sot223]
  Boreal_Networks = ESP-WROOM-32 [ESP-32S] Module [part_number=ESP-WROOM-32]
  J1 = screw terminal, 9 pins
  RELAY_5V2 = OMRON PCB Power Relay – G5LE [part_number="G5LE-1\n" package=THT]
  RELAY_5V3 = OMRON PCB Power Relay – G5LE [part_number="G5LE-1\n" package=THT]
  RELAY_5V1 = OMRON PCB Power Relay – G5LE [part_number="G5LE-1\n" package=THT]
  CAP = Tantalum Capacitor [capacitance="1 μF" voltage=16V package="D 7343 [SMD, tantalum]"]
  C___N = female pin header, 3 pins [form="♀ (female)"]
  D1 = Rectifier Diode [part_number=1N4007 package="300 mil [THT]"]
  D2 = Rectifier Diode [part_number=1N4007 package="300 mil [THT]"]
  D3 = Rectifier Diode [part_number=1N4007 package="300 mil [THT]"]
  UP = TRANSISTOR_NPN [package=to-92-ammo]
  DOWN = TRANSISTOR_NPN [package=to-92-ammo]
  MID = TRANSISTOR_NPN [package=to-92-ammo]
  EN = female pin header, 1 pin [form="♀ (female)"]
  I0 = female pin header, 1 pin [form="♀ (female)"]
  RX = female pin header, 1 pin [form="♀ (female)"]
  TX = female pin header, 1 pin [form="♀ (female)"]
  G = female pin header, 1 pin [form="♀ (female)"]

nets:
  N1: HLK-PM1.AC#0, J1.pin7, J1.pin8
  N2: HLK-PM1.AC#1, J1.pin9, RELAY_5V2.C, RELAY_5V3.C
  GND: HLK-PM1.-Vo, IC1.GND, Boreal_Networks.GND, CAP.-, UP.E, DOWN.E, MID.E, G.pin1
  N3: HLK-PM1.+Vo, IC1.IN, RELAY_5V2.COIL1, RELAY_5V3.COIL2, RELAY_5V1.COIL1, D1.cathode, D2.cathode, D3.cathode
  N4: IC1.OUT, Boreal_Networks.3V3, CAP.+, C___N.pin3
  N5: Boreal_Networks.EN, C___N.pin2
  N6: Boreal_Networks.IO0, I0.pin1
  N7: Boreal_Networks.RXD0, RX.pin1
  N8: Boreal_Networks.TXD0, TX.pin1
  N9: J1.pin5, RELAY_5V2.A
  N10: J1.pin6, RELAY_5V3.A
  N11: RELAY_5V2.COIL2, D2.anode, MID.C
  N12: RELAY_5V3.COIL1, D3.anode, DOWN.C
  N13: RELAY_5V1.COIL2, D1.anode, UP.C
  N14: C___N.pin1, EN.pin1

notes:
  SWEC
  CON1
  CON2
  AC/ N
  AC/L

custom parts:
  HLK-PM01: AC-DC 220V to 5V 5W Step-Down Power Supply Module
  ESP-WROOM-32 [ESP-32S] Module: Modulo personalizado, ESP32-S
